# Fritzing sketch robot (saved by Fritzing 0.9.3b)

parts:
  Part1 = Adafruit DC+Stepper Motor HAT [part_number="Adafruit #2348"]
  Raspberry_Pi_1 = Raspberry Pi 3 [part_number=RPI-3-V1.2]
  M1 = DC Motor
  M2 = DC Motor
  VCC1 = 4 x AAA Battery Mount
  SERVO1 = Tower Pro SG90 servo [part_number=101246]
  SPI_SSD1 = OLED 0.95" 96x64 SPI SSD1331
  Part2 = PowerBoost 1000 Basic
  BATT1 = LiPoly Battery (1300mAh)

nets:
  N1: Part1.GPIO23, SPI_SSD1.D/C
  N2: Part1.GPIO24, SPI_SSD1.RES
  N3: Part1.SPI_MOSI, Part1.SPI_CE0, Raspberry_Pi_1.GND, Raspberry_Pi_1.ID_SD, Raspberry_Pi_1.GIPO25, SPI_SSD1.DIN, SPI_SSD1.CS
  N4: Part1.SPI_SCLK, SPI_SSD1.CLK
  N5: Part1.M2A, M2.pin_1
  N6: Part1.M2B, M2.pin_2
  N7: Part1.M1B, M1.pin_1
  N8: Part1.M1A, M1.pin_2
  N9: Part1.PWM0, SERVO1.Signal
  GND: Part1.GND, VCC1.-, SERVO1.GND, SPI_SSD1.GND, Part2.GND, BATT1.negative
  N10: Part1.VMOTOR, VCC1.+
  +5V: Part1.5.0V, SERVO1.+5V, SPI_SSD1.VCC, Part2.5.0V
  N11: Part2.VBAT, BATT1.positive

custom parts:
  Adafruit DC+Stepper Motor HAT: Let your robotic dreams come true with the new DC+Stepper Motor HAT from Adafruit. This Raspberry Pi add-on is perfect for any motion project as it can drive up to 4 DC or 2 Stepper motors with full PWM speed control. Since the Raspberry Pi does not have a lot of PWM pins, we use a fully-dedicated PWM driver chip onboard to both control motor direction and speed. This chip handles all the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
  Tower Pro SG90 servo: Original file by John De Cristofaro http://www.adafruit.com/products/1449 Adafruit Feedback Servo (Small) Edited by: e-radionica.com 28/9/2015
  PowerBoost 1000 Basic: The PowerBoost 1000 is a little DC/DC boost converter module that can run from 1.8V batteries or higher, and convert the battery output to 5.2V DC for running your 5V projects. At its heart is a TPS61030 boost converter from TI. This boost converter chip has some really nice extras such as low battery detection, 4A internal switch, synchronous conversion, excellent efficiency, and 700KHz high-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
  LiPoly Battery (1300mAh): Lithium Ion Polymer Battery (1300mAh)
